// Logisim project alu.circ as structural Verilog: 1 circuit, main circuit alu
module alu (
  input  [8:0] opand1,
  input  [8:0] opand2,
  input  [8:0] size,
  input  enable,
  input  [2:0] opcode,
  output [8:0] result
);

  wire [8:0] add_1_result, div_1_p4, mul_1_result;

  add add_1 (.opand1(opand1), .opand2(opand2), .result(add_1_result));
  mul mul_1 (.opand1(opand1), .opand2(opand2), .size(size), .result(mul_1_result));
  // div div_1: pin names not known; wires that end beside it: opand1, opand2, size, div_1_p4
  Multiplexer #(.select(3), .width(9)) multiplexer_1 (
    .in1(add_1_result), .in2(mul_1_result), .in3(div_1_p4), .out(result), .sel(opcode), .en(enable));  // open: in0, in4, in5, in6, in7
endmodule
