// Logisim project cpu.circ as structural Verilog: 1 circuit, main circuit main
module main (
  output [8:0] out_1
);

  wire clock_1_out, cu_1_add, cu_1_div, cu_1_elem, cu_1_gen, cu_1_init, cu_1_ld, cu_1_ldi, cu_1_mul,
       cu_1_rst, not_1_out, or_1_out, reset_out;
  wire [8:0] alu_1_result, demultiplexer_1_out0, demultiplexer_1_out1, multiplexer_1_out, opand1_q, opand2_q,
       pc_1_line, polygen_1_dout, polygen_1_size;
  wire [11:0] ram_1_dout;

  Button reset (.out(reset_out));
  Clock clock_1 (.out(clock_1_out));
  RAM #(.addrWidth(9), .dataWidth(12), .\type ("nonvolatile")) ram_1 (
    .addr(pc_1_line), .we(1'b0), .oe(1'b1), .clk(clock_1_out), .dout(ram_1_dout));  // open: din
  pc pc_1 (
    .ldi(cu_1_ldi), .add(cu_1_add), .mul(cu_1_mul), .div(cu_1_div), .ld(cu_1_ld), .size(polygen_1_size),
    .rst(reset_out), .clk(clock_1_out), .line(pc_1_line));
  cu cu_1 (
    .opcode(ram_1_dout[11:9]), .ldi(cu_1_ldi), .add(cu_1_add), .mul(cu_1_mul), .div(cu_1_div), .ld(cu_1_ld),
    .init(cu_1_init), .gen(cu_1_gen), .rst(cu_1_rst), .elem(cu_1_elem));
  polygen polygen_1 (
    .addr(ram_1_dout[8:0]), .init(cu_1_init), .gen(cu_1_gen), .rst(cu_1_rst), .clk(clock_1_out),
    .size(polygen_1_size), .dout(polygen_1_dout));
  or or_1 (or_1_out, cu_1_add, cu_1_mul, cu_1_div);
  Multiplexer #(.enable("false"), .width(9)) multiplexer_1 (
    .in0(polygen_1_dout), .in1(ram_1_dout[8:0]), .out(multiplexer_1_out), .sel(cu_1_elem));
  Demultiplexer #(.enable("false"), .width(9)) demultiplexer_1 (
    .out0(demultiplexer_1_out0), .out1(demultiplexer_1_out1), .in(multiplexer_1_out), .sel(cu_1_ld));
  not not_1 (not_1_out, cu_1_ld);
  Register #(.trigger("high"), .width(9)) opand2 (
    .D(demultiplexer_1_out0), .en(not_1_out), .clk(clock_1_out), .Q(opand2_q));  // open: clr
  Register #(.trigger("high"), .width(9)) opand1 (
    .D(demultiplexer_1_out1), .en(cu_1_ld), .clk(clock_1_out), .Q(opand1_q));  // open: clr
  alu alu_1 (
    .opand1(opand1_q), .opand2(opand2_q), .size(polygen_1_size), .enable(or_1_out),
    .opcode(ram_1_dout[11:9]), .result(alu_1_result));
  Register #(.trigger("high"), .width(9)) register_1 (
    .D(alu_1_result), .en(or_1_out), .clk(clock_1_out), .Q(out_1));  // open: clr
endmodule
