// Logisim project mul.circ as structural Verilog: 1 circuit, main circuit mul
module mul (
  input  [3:0] in_1,
  input  [3:0] in_2,
  output [3:0] out_3
);

  wire [3:0] adder_1_out;

  Adder #(.width(4)) adder_1 (.a(in_1), .b(in_2), .out(adder_1_out));  // open: cin, cout
  assign out_3 = adder_1_out & 4'b0111;  // AND_Gate and_1, 4 bits wide
endmodule
